// Logisim project guia_0606.circ as structural Verilog: 1 circuit, main circuit main
module main (
  input  x,
  input  y,
  input  w,
  input  z,
  output out_5,
  output out_6
);

  wire and_1_out, and_2_out, and_3_out, and_4_out, and_5_out, and_6_out, not_1_out, not_2_out, not_3_out,
       not_4_out, not_5_out, not_6_out, not_7_out, not_8_out, not_9_out, not_10_out, or_1_out, or_2_out;

  not not_1 (not_1_out, y);
  not not_2 (not_2_out, x);
  not not_3 (not_3_out, w);
  not not_4 (not_4_out, w);
  not not_5 (not_5_out, y);
  not not_6 (not_6_out, z);
  or or_1 (or_1_out, not_1_out, w, not_2_out);
  and and_1 (and_1_out, y, not_3_out, x);
  and and_2 (and_2_out, z, w, y);
  or or_2 (or_2_out, and_2_out, not_7_out);
  not not_7 (not_7_out, x);
  and and_3 (and_3_out, not_4_out, x);
  and and_4 (and_4_out, x, not_5_out, w);
  and and_5 (and_5_out, x, w, not_6_out);
  not not_8 (not_8_out, or_1_out);
  not not_9 (not_9_out, and_1_out);
  not not_10 (not_10_out, or_2_out);
  or or_3 (out_6, and_3_out, and_4_out, and_5_out);
  and and_6 (and_6_out, not_8_out, not_9_out);
  or or_4 (out_5, and_6_out, not_10_out);
endmodule
