// Logisim project aula_sexta_23092022.circ as structural Verilog
module subtrator (
  input  x,
  input  y,
  output s0,
  output s1
);

  wire not_1_out;

  not not_1 (not_1_out, x);
  xor xor_1 (s0, x, y);
  and and_1 (s1, not_1_out, y);
endmodule

module subtrator_3bits (
  input  a,
  input  b,
  input  c,
  output out_4
);

  wire and_1_out, and_2_out, and_3_out, not_1_out;

  not not_1 (not_1_out, a);
  and and_1 (and_1_out, c, not_1_out);
  and and_2 (and_2_out, not_1_out, b);
  and and_3 (and_3_out, b, c);
  or or_1 (out_4, and_1_out, and_2_out, and_3_out);
endmodule
