// Logisim project soma.circ as structural Verilog
module SoP__1 (
  input  a,
  input  b,
  output out_3,
  output out_4
);

  wire and_1_out, and_2_out, not_1_out, not_2_out;

  not not_1 (not_1_out, a);
  not not_2 (not_2_out, b);
  and and_1 (and_1_out, not_1_out, b);
  or or_1 (out_3, and_1_out, and_2_out);
  and and_2 (and_2_out, not_2_out, a);
  and and_3 (out_4, b, a);
endmodule

module HA_compacto (
  input  a,
  input  b,
  output out_3,
  output out_4
);

  xor xor_1 (out_3, b, a);
  and and_1 (out_4, b, a);
endmodule

module FA__1 (
  input  a,
  input  b,
  input  v,
  output out_4,
  output out_5
);

  wire and_1_out, and_2_out, and_3_out, and_4_out, and_5_out, and_6_out, and_7_out, and_8_out, not_1_out,
       not_2_out, not_3_out;

  not not_1 (not_1_out, a);
  not not_2 (not_2_out, b);
  not not_3 (not_3_out, v);
  and and_1 (and_1_out, not_1_out, not_2_out, v);
  and and_2 (and_2_out, not_1_out, b, not_3_out);
  and and_3 (and_3_out, a, not_2_out, not_3_out);
  and and_4 (and_4_out, a, b, v);
  and and_5 (and_5_out, not_1_out, b, v);
  and and_6 (and_6_out, a, not_2_out, v);
  and and_7 (and_7_out, a, b, not_3_out);
  and and_8 (and_8_out, a, b, v);
  or or_1 (out_4, and_1_out, and_2_out, and_3_out, and_4_out);
  or or_2 (out_5, and_5_out, and_6_out, and_7_out, and_8_out);
endmodule
