// Logisim project guia08_v01.circ as structural Verilog: 1 circuit, main circuit main
module main (
  input  A,
  input  B,
  input  A_2,
  input  B_2,
  input  VEM,
  output SAIDA_S,
  output SAIDA_V,
  output SAIDA_S_2,
  output SAIDA_V_2
);

  wire and_1_out, and_2_out, and_3_out, and_4_out, and_5_out, and_6_out, and_7_out, and_8_out, and_9_out,
       and_10_out, not_1_out, not_2_out, not_3_out, not_4_out, not_5_out;

  not not_1 (not_1_out, A);
  not not_2 (not_2_out, B_2);
  not not_3 (not_3_out, A_2);
  not not_4 (not_4_out, B);
  not not_5 (not_5_out, VEM);
  and and_1 (and_1_out, not_3_out, not_2_out, VEM);
  and and_2 (and_2_out, not_3_out, B_2, not_5_out);
  and and_3 (and_3_out, A_2, not_2_out, not_5_out);
  and and_4 (and_4_out, A_2, B_2, VEM);
  and and_5 (and_5_out, not_3_out, B_2, VEM);
  and and_6 (and_6_out, A_2, not_2_out, VEM);
  and and_7 (and_7_out, A_2, B_2, not_5_out);
  and and_8 (and_8_out, A_2, B_2, VEM);
  and and_9 (and_9_out, not_1_out, B);
  or or_1 (SAIDA_S, and_9_out, and_10_out);
  and and_10 (and_10_out, A, not_4_out);
  and and_11 (SAIDA_V, A, B);
  or or_2 (SAIDA_S_2, and_1_out, and_2_out, and_3_out, and_4_out);
  or or_3 (SAIDA_V_2, and_5_out, and_6_out, and_7_out, and_8_out);

  // Notes on the sheet:
  //   V = (A.B)
  //   S = (A'.B) + (A.B')
  //   S = (A'.B'.VEM) + (A'.B.VEM') + (A.B'.VEM') + (A.B.VEM)
  //   VAI = (A'.B.VEM) + (A.B'.VEM) + (A.B.VEM') + (A.B.VEM)
endmodule
